// Logisim project ULA.circ as structural Verilog: 27 circuits, main circuit main
module main (
  input  _0,
  input  _0_2,
  input  [2:0] in_3,
  input  in_4,
  input  in_5,
  input  _1,
  input  _1_2,
  input  in_8,
  input  in_9,
  input  _1_3,
  input  in_11,
  input  in_12,
  input  [4:0] _01010,
  input  [4:0] _01010_2,
  input  [4:0] A,
  input  _1_4,
  input  [4:0] B,
  input  in_18,
  input  in_19,
  input  _1_5,
  input  _1_6,
  input  in_22,
  input  in_23,
  input  _0_3,
  input  _1_7,
  input  _1_8,
  input  in_27,
  input  _0_4,
  input  _0_5,
  output [4:0] out_30,
  output [4:0] out_31
);

  wire _5bit_comparator_a___b, _5bt_comparator_a___b, _5it_comparator_a___b, _7_decoder_2_a_2,
       _7_decoder_2_b_2, _7_decoder_2_c_2, _7_decoder_2_d_2, _7_decoder_2_e, _7_decoder_2_f, _7_decoder_2_g,
       _7_decoder_a_2, _7_decoder_b_2, _7_decoder_c_2, _7_decoder_d_2, _7_decoder_e, _7_decoder_f,
       _7_decoder_g, _7decoder_2_a_2, _7decoder_2_b_2, _7decoder_2_c_2, _7decoder_2_d_2, _7decoder_2_e,
       _7decoder_2_f, _7decoder_2_g, _7decoder_3_a_2, _7decoder_3_b_2, _7decoder_3_c_2, _7decoder_3_d_2,
       _7decoder_3_e, _7decoder_3_f, _7decoder_3_g, _7decoder_a_2, _7decoder_b_2, _7decoder_c_2,
       _7decoder_d_2, _7decoder_e, _7decoder_f, _7decoder_g, adder_p1, adder_p4, and_1_out, and_2_out,
       and_3_out, and_4_out, greater_than_out_6, less_or_equal_to_out_7, n7_segment_decoder_1_a_2,
       n7_segment_decoder_1_b_2, n7_segment_decoder_1_c_2, n7_segment_decoder_1_d_2, n7_segment_decoder_1_e,
       n7_segment_decoder_1_f, n7_segment_decoder_1_g, not_1_out, not_2_out, not_3_out, not_4_out, not_5_out,
       or_1_out, or_2_out, subtractor_overflow;
  wire [4:0] _2x1_mult_2_out_4, _2x1_mult_out_4, _5bit_sub_output, _5bit_subtractor_output, C2_format_output,
       greater_than_output, less_or_equal_to_output, min_out_6, subtractor_2_output, subtractor_output;

  _7_Segment_Display u_7_segment_display_1 (
    .g(_7decoder_3_g), .f(_7decoder_3_f), .a(_7decoder_3_a_2), .b(_7decoder_3_b_2), .e(_7decoder_3_e),
    .d(_7decoder_3_d_2), .c(_7decoder_3_c_2));  // open: dp
  _7_Segment_Display u_7_segment_display_2 (
    .g(_7decoder_g), .f(_7decoder_f), .a(_7decoder_a_2), .b(_7decoder_b_2), .e(_7decoder_e),
    .d(_7decoder_d_2), .c(_7decoder_c_2));  // open: dp
  _7_segment_decoder _7decoder (
    .A(_0_2), .B(_0_2), .C(_0_2), .D(not_1_out), .a_2(_7decoder_a_2), .b_2(_7decoder_b_2),
    .c_2(_7decoder_c_2), .d_2(_7decoder_d_2), .e(_7decoder_e), .f(_7decoder_f), .g(_7decoder_g));
  not not_1 (not_1_out, _5it_comparator_a___b);
  _5bit_subtractor _5bit_sub (.\output (_5bit_sub_output), .m(_1_7), .A(B), .B(_01010_2));  // open: Overflow
  not not_2 (not_2_out, _5bit_comparator_a___b);
  _7_segment_decoder _7decoder_2 (
    .A(_0_5), .B(_0_5), .C(_0_5), .D(not_2_out), .a_2(_7decoder_2_a_2), .b_2(_7decoder_2_b_2),
    .c_2(_7decoder_2_c_2), .d_2(_7decoder_2_d_2), .e(_7decoder_2_e), .f(_7decoder_2_f), .g(_7decoder_2_g));
  _5bit_2x1_multiplexer _2x1_mult (
    .A(A), .B(_5bit_subtractor_output), .Seletor(_5it_comparator_a___b), .out_4(_2x1_mult_out_4));
  _5bit_subtractor _5bit_subtractor (
    .\output (_5bit_subtractor_output), .m(_1), .A(A), .B(_01010_2));  // open: Overflow
  _5bit_comparator _5bit_comparator (
    .left_less(in_27), .left_greater(in_27), .left_equal(_1_7), .A___B(_5bit_comparator_a___b), .A(B),
    .B(_01010_2));  // open: A___B_2, A___B_3
  _5bit_2x1_multiplexer _2x1_mult_2 (
    .A(B), .B(_5bit_sub_output), .Seletor(_5bit_comparator_a___b), .out_4(_2x1_mult_2_out_4));
  _7_Segment_Display u_7_segment_display_3 (
    .g(_7_decoder_g), .f(_7_decoder_f), .a(_7_decoder_a_2), .b(_7_decoder_b_2), .e(_7_decoder_e),
    .d(_7_decoder_d_2), .c(_7_decoder_c_2));  // open: dp
  _7_Segment_Display u_7_segment_display_4 (
    .g(_7decoder_2_g), .f(_7decoder_2_f), .a(_7decoder_2_a_2), .b(_7decoder_2_b_2), .e(_7decoder_2_e),
    .d(_7decoder_2_d_2), .c(_7decoder_2_c_2));  // open: dp
  _7_segment_decoder _7decoder_3 (
    .A(_2x1_mult_out_4[3]), .B(_2x1_mult_out_4[2]), .C(_2x1_mult_out_4[1]), .D(_2x1_mult_out_4[0]),
    .a_2(_7decoder_3_a_2), .b_2(_7decoder_3_b_2), .c_2(_7decoder_3_c_2), .d_2(_7decoder_3_d_2),
    .e(_7decoder_3_e), .f(_7decoder_3_f), .g(_7decoder_3_g));
  _5bit_comparator _5it_comparator (
    .left_less(in_4), .left_greater(in_5), .left_equal(_1), .A___B(_5it_comparator_a___b), .A(A), .B(_01010_2));  // open: A___B_2, A___B_3
  _7_segment_decoder _7_decoder (
    .A(_2x1_mult_2_out_4[3]), .B(_2x1_mult_2_out_4[2]), .C(_2x1_mult_2_out_4[1]), .D(_2x1_mult_2_out_4[0]),
    .a_2(_7_decoder_a_2), .b_2(_7_decoder_b_2), .c_2(_7_decoder_c_2), .d_2(_7_decoder_d_2), .e(_7_decoder_e),
    .f(_7_decoder_f), .g(_7_decoder_g));
  C2_format C2_format (.Input(A), .Aux(_0), .Output(C2_format_output));
  greater_than greater_than (
    .left_less(in_9), .left_greater(in_8), .left_equal(_1_2), .out_6(greater_than_out_6), .A(A), .B(B),
    .Output(greater_than_output));
  less_or_equal_to less_or_equal_to (
    .left_less(in_12), .left_greater(in_11), .left_equal(_1_3), .out_7(less_or_equal_to_out_7), .A(A), .B(B),
    .\output (less_or_equal_to_output));
  min min (.left_less(in_23), .left_greater(in_22), .left_equal(_1_6), .A(A), .B(B), .out_6(min_out_6));
  _5bit_subtractor subtractor (.\output (subtractor_output), .m(_1_8), .Overflow(subtractor_overflow), .A(A), .B(B));
  // _5bit_adder adder: pin names not known; wires that end beside it: adder_p1, B, A, adder_p4, _0_4
  and and_1 (and_1_out, greater_than_out_6, and_3_out);
  and and_2 (and_2_out, less_or_equal_to_out_7, and_4_out);
  and and_3 (and_3_out, in_3[2], not_3_out, not_4_out);
  not not_3 (not_3_out, in_3[1]);
  not not_4 (not_4_out, in_3[0]);
  or or_1 (or_1_out, subtractor_overflow, adder_p1);
  LED LED_OVERFLOW (.in(or_1_out));
  and and_4 (and_4_out, in_3[1], in_3[0]);
  // _5bit_8x1_multiplexer _8x1_mult: pin names not known; wires that end beside it: C2_format_output, greater_than_output, less_or_equal_to_output, min_out_6, subtractor_output, adder_p4, in_3, out_30
  or or_2 (or_2_out, and_1_out, and_2_out);
  LED LED_STATUS (.in(or_2_out));
  _5bit_comparator _5bt_comparator (
    .left_less(in_19), .left_greater(in_18), .left_equal(_1_4), .A___B(_5bt_comparator_a___b), .A(out_30),
    .B(_01010));  // open: A___B_2, A___B_3
  _5bit_2x1_multiplexer _2x1mult (.A(out_30), .B(subtractor_2_output), .Seletor(_5bt_comparator_a___b), .out_4(out_31));
  not not_5 (not_5_out, _5bt_comparator_a___b);
  _7_segment_decoder _7_decoder_2 (
    .A(_0_3), .B(_0_3), .C(_0_3), .D(not_5_out), .a_2(_7_decoder_2_a_2), .b_2(_7_decoder_2_b_2),
    .c_2(_7_decoder_2_c_2), .d_2(_7_decoder_2_d_2), .e(_7_decoder_2_e), .f(_7_decoder_2_f), .g(_7_decoder_2_g));
  _7_Segment_Display u_7_segment_display_5 (
    .g(_7_decoder_2_g), .f(_7_decoder_2_f), .a(_7_decoder_2_a_2), .b(_7_decoder_2_b_2), .e(_7_decoder_2_e),
    .d(_7_decoder_2_d_2), .c(_7_decoder_2_c_2));  // open: dp
  _7_Segment_Display u_7_segment_display_6 (
    .g(n7_segment_decoder_1_g), .f(n7_segment_decoder_1_f), .a(n7_segment_decoder_1_a_2),
    .b(n7_segment_decoder_1_b_2), .e(n7_segment_decoder_1_e), .d(n7_segment_decoder_1_d_2),
    .c(n7_segment_decoder_1_c_2));  // open: dp
  _5bit_subtractor subtractor_2 (.\output (subtractor_2_output), .m(_1_5), .A(out_30), .B(_01010));  // open: Overflow
  LED LED_NEGATIVO (.in(out_31[4]));
  _7_segment_decoder u_7_segment_decoder_1 (
    .A(out_31[3]), .B(out_31[2]), .C(out_31[1]), .D(out_31[0]), .a_2(n7_segment_decoder_1_a_2),
    .b_2(n7_segment_decoder_1_b_2), .c_2(n7_segment_decoder_1_c_2), .d_2(n7_segment_decoder_1_d_2),
    .e(n7_segment_decoder_1_e), .f(n7_segment_decoder_1_f), .g(n7_segment_decoder_1_g));

  // Notes on the sheet:
  //   7 decoder
endmodule

module half_adder (
  input  A,
  input  B,
  output Carry_out,
  output Soma
);

  and and_1 (Carry_out, B, A);
  xor xor_1 (Soma, A, B);
endmodule

module full_adder (
  input  A,
  input  B,
  input  Carry_in,
  output Carry_out,
  output Soma
);

  wire half_adder_2_carry_out, half_adder_carry_out, half_adder_soma;

  half_adder half_adder (.A(A), .B(B), .Carry_out(half_adder_carry_out), .Soma(half_adder_soma));
  half_adder half_adder_2 (.A(half_adder_soma), .B(Carry_in), .Carry_out(half_adder_2_carry_out), .Soma(Soma));
  or or_1 (Carry_out, half_adder_carry_out, half_adder_2_carry_out);
endmodule

module C2_format (
  input  [4:0] Input,
  input  Aux,
  output [4:0] Output
);

  wire full_adder_1_carry_out, full_adder_2_carry_out, full_adder_3_carry_out, full_adder_4_carry_out,
       not_1_out, not_2_out, not_3_out, not_4_out, not_5_out, not_6_out, not_7_out, xor_1_out, xor_2_out,
       xor_3_out, xor_4_out, xor_5_out;

  not not_1 (not_1_out, Input[0]);
  not not_2 (not_2_out, Input[1]);
  not not_3 (not_3_out, Input[2]);
  not not_4 (not_4_out, Input[3]);
  not not_5 (not_5_out, Input[4]);
  not not_6 (not_6_out, Input[4]);
  not not_7 (not_7_out, not_6_out);
  xor xor_1 (xor_1_out, not_1_out, not_6_out);
  xor xor_2 (xor_2_out, not_2_out, not_6_out);
  xor xor_3 (xor_3_out, not_3_out, not_6_out);
  xor xor_4 (xor_4_out, not_4_out, not_6_out);
  xor xor_5 (xor_5_out, not_5_out, not_6_out);
  full_adder full_adder_1 (
    .A(xor_1_out), .B(not_7_out), .Carry_in(Aux), .Carry_out(full_adder_1_carry_out), .Soma(Output[0]));
  full_adder full_adder_2 (
    .A(xor_2_out), .B(Aux), .Carry_in(full_adder_1_carry_out), .Carry_out(full_adder_2_carry_out),
    .Soma(Output[1]));
  full_adder full_adder_3 (
    .A(xor_3_out), .B(Aux), .Carry_in(full_adder_2_carry_out), .Carry_out(full_adder_3_carry_out),
    .Soma(Output[2]));
  full_adder full_adder_4 (
    .A(xor_4_out), .B(Aux), .Carry_in(full_adder_3_carry_out), .Carry_out(full_adder_4_carry_out),
    .Soma(Output[3]));
  full_adder full_adder_5 (
    .A(xor_5_out), .B(Aux), .Carry_in(full_adder_4_carry_out), .Soma(Output[4]));  // open: Carry_out
endmodule

module _1bit_comparator (
  input  A,
  input  B,
  input  in_equal,
  input  in_greater_than,
  input  in_less_than,
  output A___B,
  output A___B_2,
  output A___B_3
);

  wire and_1_out, and_2_out, not_1_out, not_2_out, xnor_1_out;

  not not_1 (not_1_out, B);
  not not_2 (not_2_out, A);
  xnor xnor_1 (xnor_1_out, A, B);
  and and_1 (and_1_out, A, in_equal, not_1_out);
  and and_2 (and_2_out, not_2_out, in_equal, B);
  and and_3 (A___B, xnor_1_out, in_equal);
  or or_1 (A___B_2, in_greater_than, and_1_out);
  or or_2 (A___B_3, in_less_than, and_2_out);
endmodule

module _5bit_comparator (
  input  left_less,
  input  left_greater,
  input  left_equal,
  input  [4:0] A,
  input  [4:0] B,
  output A___B,
  output A___B_2,
  output A___B_3
);

  wire n1bit_comparator_1_a___b, n1bit_comparator_1_a___b_2, n1bit_comparator_1_a___b_3,
       n1bit_comparator_2_a___b, n1bit_comparator_2_a___b_2, n1bit_comparator_2_a___b_3,
       n1bit_comparator_3_a___b, n1bit_comparator_3_a___b_2, n1bit_comparator_3_a___b_3,
       n1bit_comparator_4_a___b, n1bit_comparator_4_a___b_2, n1bit_comparator_4_a___b_3, not_1_out, not_2_out;

  _1bit_comparator u_1bit_comparator_1 (
    .A(not_2_out), .B(not_1_out), .in_equal(left_equal), .in_greater_than(left_greater),
    .in_less_than(left_less), .A___B(n1bit_comparator_1_a___b), .A___B_2(n1bit_comparator_1_a___b_2),
    .A___B_3(n1bit_comparator_1_a___b_3));
  _1bit_comparator u_1bit_comparator_2 (
    .A(A[3]), .B(B[3]), .in_equal(n1bit_comparator_1_a___b), .in_greater_than(n1bit_comparator_1_a___b_2),
    .in_less_than(n1bit_comparator_1_a___b_3), .A___B(n1bit_comparator_2_a___b),
    .A___B_2(n1bit_comparator_2_a___b_2), .A___B_3(n1bit_comparator_2_a___b_3));
  _1bit_comparator u_1bit_comparator_3 (
    .A(A[2]), .B(B[2]), .in_equal(n1bit_comparator_2_a___b), .in_greater_than(n1bit_comparator_2_a___b_2),
    .in_less_than(n1bit_comparator_2_a___b_3), .A___B(n1bit_comparator_3_a___b),
    .A___B_2(n1bit_comparator_3_a___b_2), .A___B_3(n1bit_comparator_3_a___b_3));
  _1bit_comparator u_1bit_comparator_4 (
    .A(A[1]), .B(B[1]), .in_equal(n1bit_comparator_3_a___b), .in_greater_than(n1bit_comparator_3_a___b_2),
    .in_less_than(n1bit_comparator_3_a___b_3), .A___B(n1bit_comparator_4_a___b),
    .A___B_2(n1bit_comparator_4_a___b_2), .A___B_3(n1bit_comparator_4_a___b_3));
  not not_1 (not_1_out, B[4]);
  not not_2 (not_2_out, A[4]);
  _1bit_comparator u_1bit_comparator_5 (
    .A(A[0]), .B(B[0]), .in_equal(n1bit_comparator_4_a___b), .in_greater_than(n1bit_comparator_4_a___b_2),
    .in_less_than(n1bit_comparator_4_a___b_3), .A___B(A___B_3), .A___B_2(A___B_2), .A___B_3(A___B));
endmodule

module _5bit_adder (
  input  [7:0] A,
  input  [7:0] B,
  output [7:0] \output 
);

  wire full_adder_2_carry_out, full_adder_3_carry_out, full_adder_4_carry_out, full_adder_5_carry_out,
       full_adder_6_carry_out, full_adder_7_carry_out, half_adder_1_carry_out;

  full_adder full_adder_1 (
    .A(A[7]), .B(B[7]), .Carry_in(full_adder_2_carry_out), .Soma(\output [7]));  // open: Carry_out
  full_adder full_adder_2 (
    .A(A[6]), .B(B[6]), .Carry_in(full_adder_3_carry_out), .Carry_out(full_adder_2_carry_out),
    .Soma(\output [6]));
  full_adder full_adder_3 (
    .A(A[5]), .B(B[5]), .Carry_in(full_adder_4_carry_out), .Carry_out(full_adder_3_carry_out),
    .Soma(\output [5]));
  full_adder full_adder_4 (
    .A(A[4]), .B(B[4]), .Carry_in(full_adder_6_carry_out), .Carry_out(full_adder_4_carry_out),
    .Soma(\output [4]));
  full_adder full_adder_5 (
    .A(A[2]), .B(B[2]), .Carry_in(full_adder_7_carry_out), .Carry_out(full_adder_5_carry_out),
    .Soma(\output [2]));
  full_adder full_adder_6 (
    .A(A[3]), .B(B[3]), .Carry_in(full_adder_5_carry_out), .Carry_out(full_adder_6_carry_out),
    .Soma(\output [3]));
  full_adder full_adder_7 (
    .A(A[1]), .B(B[1]), .Carry_in(half_adder_1_carry_out), .Carry_out(full_adder_7_carry_out),
    .Soma(\output [1]));
  half_adder half_adder_1 (.A(A[0]), .B(B[0]), .Carry_out(half_adder_1_carry_out), .Soma(\output [0]));
endmodule

module _5bit_subtractor (
  input  m,
  input  [4:0] A,
  input  [4:0] B,
  output [4:0] \output ,
  output Overflow
);

  wire full_adder_1_carry_out, full_adder_2_carry_out, full_adder_3_carry_out, full_adder_4_carry_out,
       full_adder_5_carry_out, xor_2_out, xor_3_out, xor_4_out, xor_5_out, xor_6_out;

  xor xor_1 (Overflow, full_adder_1_carry_out, full_adder_2_carry_out);
  full_adder full_adder_1 (
    .A(A[3]), .B(xor_5_out), .Carry_in(full_adder_3_carry_out), .Carry_out(full_adder_1_carry_out),
    .Soma(\output [3]));
  full_adder full_adder_2 (
    .A(A[4]), .B(xor_6_out), .Carry_in(full_adder_1_carry_out), .Carry_out(full_adder_2_carry_out),
    .Soma(\output [4]));
  full_adder full_adder_3 (
    .A(A[2]), .B(xor_4_out), .Carry_in(full_adder_5_carry_out), .Carry_out(full_adder_3_carry_out),
    .Soma(\output [2]));
  full_adder full_adder_4 (
    .A(A[0]), .B(xor_2_out), .Carry_in(m), .Carry_out(full_adder_4_carry_out), .Soma(\output [0]));
  full_adder full_adder_5 (
    .A(A[1]), .B(xor_3_out), .Carry_in(full_adder_4_carry_out), .Carry_out(full_adder_5_carry_out),
    .Soma(\output [1]));
  xor xor_2 (xor_2_out, B[0], m);
  xor xor_3 (xor_3_out, B[1], m);
  xor xor_4 (xor_4_out, B[2], m);
  xor xor_5 (xor_5_out, B[3], m);
  xor xor_6 (xor_6_out, B[4], m);
endmodule

module min (
  input  left_less,
  input  left_greater,
  input  left_equal,
  input  [4:0] A,
  input  [4:0] B,
  output [4:0] out_6
);

  wire and_1_out, n5bit_comparator_1_a___b, n5bit_comparator_1_a___b_2, n5bit_comparator_1_a___b_3,
       not_1_out, or_1_out;

  not not_1 (not_1_out, n5bit_comparator_1_a___b);
  and and_1 (and_1_out, not_1_out, or_1_out);
  _5bit_comparator u_5bit_comparator_1 (
    .left_less(left_less), .left_greater(left_greater), .left_equal(left_equal),
    .A___B(n5bit_comparator_1_a___b), .A___B_2(n5bit_comparator_1_a___b_2),
    .A___B_3(n5bit_comparator_1_a___b_3), .A(A), .B(B));
  or or_1 (or_1_out, n5bit_comparator_1_a___b_2, n5bit_comparator_1_a___b_3);
  _5bit_2x1_multiplexer u_5bit_2x1_multiplexer_1 (.A(B), .B(A), .Seletor(and_1_out), .out_4(out_6));
endmodule

module _2x1_multiplexer (
  input  A,
  input  B,
  input  Seletor,
  output out_4
);

  wire and_1_out, and_2_out, not_1_out;

  not not_1 (not_1_out, Seletor);
  and and_1 (and_1_out, A, not_1_out);
  and and_2 (and_2_out, Seletor, B);
  or or_1 (out_4, and_1_out, and_2_out);
endmodule

module _5bit_2x1_multiplexer (
  input  [4:0] A,
  input  [4:0] B,
  input  Seletor,
  output [4:0] out_4
);

  wire not_1_out;

  not not_1 (not_1_out, Seletor);
  _2x1_multiplexer u_2x1_multiplexer_1 (.A(A[0]), .B(B[0]), .Seletor(not_1_out), .out_4(out_4[0]));
  _2x1_multiplexer u_2x1_multiplexer_2 (.A(A[1]), .B(B[1]), .Seletor(not_1_out), .out_4(out_4[1]));
  _2x1_multiplexer u_2x1_multiplexer_3 (.A(A[2]), .B(B[2]), .Seletor(not_1_out), .out_4(out_4[2]));
  _2x1_multiplexer u_2x1_multiplexer_4 (.A(A[3]), .B(B[3]), .Seletor(not_1_out), .out_4(out_4[3]));
  _2x1_multiplexer u_2x1_multiplexer_5 (.A(A[4]), .B(B[4]), .Seletor(not_1_out), .out_4(out_4[4]));
endmodule

module _5bit_4x1_multiplexer (
  input  Seletor1,
  input  Seletor2,
  input  [4:0] A,
  input  [4:0] B,
  input  [4:0] C,
  input  [4:0] D,
  output [4:0] out_7
);

  wire [4:0] n5bit_2x1_multiplexer_1_out_4, n5bit_2x1_multiplexer_2_out_4;

  _5bit_2x1_multiplexer u_5bit_2x1_multiplexer_1 (
    .A(A), .B(B), .Seletor(Seletor1), .out_4(n5bit_2x1_multiplexer_1_out_4));
  _5bit_2x1_multiplexer u_5bit_2x1_multiplexer_2 (
    .A(C), .B(D), .Seletor(Seletor1), .out_4(n5bit_2x1_multiplexer_2_out_4));
  _5bit_2x1_multiplexer u_5bit_2x1_multiplexer_3 (
    .A(n5bit_2x1_multiplexer_1_out_4), .B(n5bit_2x1_multiplexer_2_out_4), .Seletor(Seletor2), .out_4(out_7));
endmodule

module _5bit_8x1_multiplexer (
  input  [2:0] Seletor,
  input  [4:0] A,
  input  [4:0] B,
  input  [4:0] C,
  input  [4:0] D,
  input  [4:0] E,
  input  [4:0] F,
  input  [4:0] G,
  input  [4:0] H,
  output [4:0] out_10
);

  wire [4:0] n5bit_4x1_multiplexer_1_out_7, n5bit_4x1_multiplexer_2_out_7;

  _5bit_4x1_multiplexer u_5bit_4x1_multiplexer_1 (
    .A(A), .B(B), .C(C), .D(D), .Seletor1(Seletor[0]), .Seletor2(Seletor[1]),
    .out_7(n5bit_4x1_multiplexer_1_out_7));
  _5bit_4x1_multiplexer u_5bit_4x1_multiplexer_2 (
    .A(E), .B(F), .C(G), .D(H), .Seletor1(Seletor[0]), .Seletor2(Seletor[1]),
    .out_7(n5bit_4x1_multiplexer_2_out_7));
  _5bit_2x1_multiplexer u_5bit_2x1_multiplexer_1 (
    .A(n5bit_4x1_multiplexer_1_out_7), .B(n5bit_4x1_multiplexer_2_out_7), .Seletor(Seletor[2]), .out_4(out_10));
endmodule

module less_or_equal_to (
  input  left_less,
  input  left_equal,
  input  left_greater,
  input  [4:0] A,
  input  [4:0] B,
  output [4:0] \output ,
  output out_7
);

  wire n5bit_comparator_1_a___b, n5bit_comparator_1_a___b_3;

  _5bit_comparator u_5bit_comparator_1 (
    .left_less(left_less), .left_greater(left_greater), .left_equal(left_equal),
    .A___B(n5bit_comparator_1_a___b), .A___B_3(n5bit_comparator_1_a___b_3), .A(A), .B(B));  // open: A___B_2
  or or_1 (out_7, n5bit_comparator_1_a___b, n5bit_comparator_1_a___b_3);

  assign \output  = A;
endmodule

module greater_than (
  input  left_less,
  input  left_equal,
  input  left_greater,
  input  [4:0] A,
  input  [4:0] B,
  output out_6,
  output [4:0] Output
);

  _5bit_comparator u_5bit_comparator_1 (
    .left_less(left_less), .left_greater(left_greater), .left_equal(left_equal), .A___B_2(out_6), .A(A), .B(B));  // open: A___B, A___B_3

  assign Output = A;
endmodule

module _7_segment_decoder (
  input  A,
  input  B,
  input  C,
  input  D,
  output a_2,
  output b_2,
  output c_2,
  output d_2,
  output e,
  output f,
  output g
);

  wire and_1_out, and_2_out, and_3_out, and_4_out, and_5_out, and_6_out, and_7_out, and_8_out, and_9_out,
       and_10_out, not_1_out, not_2_out, not_3_out, xnor_1_out, xnor_2_out, xor_1_out;

  not not_1 (not_1_out, B);
  not not_2 (not_2_out, C);
  not not_3 (not_3_out, D);
  and and_1 (and_1_out, C, not_3_out);
  and and_2 (and_2_out, not_1_out, C);
  and and_3 (and_3_out, not_1_out, not_3_out);
  and and_4 (and_4_out, B, not_2_out, D);
  and and_5 (and_5_out, C, not_3_out);
  and and_6 (and_6_out, not_1_out, not_3_out);
  and and_7 (and_7_out, not_2_out, not_3_out);
  and and_8 (and_8_out, B, not_3_out);
  and and_9 (and_9_out, B, not_2_out);
  xor xor_1 (xor_1_out, B, C);
  and and_10 (and_10_out, B, not_3_out);
  xnor xnor_1 (xnor_1_out, B, D);
  xnor xnor_2 (xnor_2_out, C, D);
  or or_1 (a_2, A, C, xnor_1_out);
  or or_2 (b_2, not_1_out, xnor_2_out);
  or or_3 (c_2, not_2_out, D, B);
  or or_4 (d_2, and_1_out, and_2_out, and_3_out, and_4_out);
  or or_5 (e, and_5_out, and_6_out);
  or or_6 (f, and_7_out, and_8_out, A, and_9_out);
  or or_7 (g, xor_1_out, A, and_10_out);
endmodule

module shift_bit (
  input  [4:0] A,
  output [4:0] out_2
);

  D_Flip_Flop d_ff_1 (.clk(A[4]), .Q(out_2[0]));  // open: D, Qn, preset, en, reset

  assign out_2[4:1] = A[3:0];
endmodule

module shift_bit_n_times (
  input  in_1,
  input  [4:0] in_2,
  input  [4:0] in_3,
  input  [4:0] in_4,
  input  [4:0] in_5,
  input  [4:0] in_6,
  input  [4:0] in_7,
  input  [4:0] in_8,
  input  [4:0] in_9,
  input  [4:0] in_10,
  input  [4:0] in_11,
  input  [4:0] A,
  input  [4:0] B,
  input  in_14,
  input  in_15,
  input  [4:0] in_16,
  input  [4:0] in_17,
  input  [4:0] in_18,
  input  [4:0] in_19,
  output [4:0] \output 
);

  wire and_1_out, or_1_out;
  wire [4:0] shift_aux_1_out_6, shift_aux_2_out_6, shift_aux_3_out_6, shift_aux_4_out_6, shift_aux_5_out_6,
       shift_aux_6_out_6, shift_aux_7_out_6, shift_aux_9_out_6, shift_aux_10_out_6, shift_aux_11_out_6,
       shift_aux_12_out_6, shift_aux_13_out_6, shift_aux_14_out_6, shift_bit_1_out_2;

  or or_1 (or_1_out, B[0], B[1], B[2], B[3], B[4]);
  and and_1 (and_1_out, or_1_out, in_1);
  shift_bit shift_bit_1 (.A(A), .out_2(shift_bit_1_out_2));
  shift_aux shift_aux_1 (
    .B(B), .A(shift_bit_1_out_2), .current(in_2), .in_4(in_14), .in_5(in_15), .out_6(shift_aux_1_out_6));
  shift_aux shift_aux_2 (
    .B(B), .A(shift_aux_14_out_6), .current(in_16), .in_4(in_14), .in_5(in_15), .out_6(shift_aux_2_out_6));
  shift_aux shift_aux_3 (
    .B(B), .A(shift_aux_2_out_6), .current(in_17), .in_4(in_14), .in_5(in_15), .out_6(shift_aux_3_out_6));
  shift_aux shift_aux_4 (
    .B(B), .A(shift_aux_1_out_6), .current(in_3), .in_4(in_14), .in_5(in_15), .out_6(shift_aux_4_out_6));
  shift_aux shift_aux_5 (
    .B(B), .A(shift_aux_4_out_6), .current(in_4), .in_4(in_14), .in_5(in_15), .out_6(shift_aux_5_out_6));
  shift_aux shift_aux_6 (
    .B(B), .A(shift_aux_3_out_6), .current(in_18), .in_4(in_14), .in_5(in_15), .out_6(shift_aux_6_out_6));
  shift_aux shift_aux_7 (
    .B(B), .A(shift_aux_5_out_6), .current(in_5), .in_4(in_14), .in_5(in_15), .out_6(shift_aux_7_out_6));
  shift_aux shift_aux_8 (.B(B), .A(shift_aux_6_out_6), .current(in_19), .in_4(in_14), .in_5(in_15), .out_6(\output ));
  shift_aux shift_aux_9 (
    .B(B), .A(shift_aux_7_out_6), .current(in_6), .in_4(in_14), .in_5(in_15), .out_6(shift_aux_9_out_6));
  shift_aux shift_aux_10 (
    .B(B), .A(shift_aux_9_out_6), .current(in_7), .in_4(in_14), .in_5(in_15), .out_6(shift_aux_10_out_6));
  shift_aux shift_aux_11 (
    .B(B), .A(shift_aux_10_out_6), .current(in_8), .in_4(in_14), .in_5(in_15), .out_6(shift_aux_11_out_6));
  shift_aux shift_aux_12 (
    .B(B), .A(shift_aux_11_out_6), .current(in_9), .in_4(in_14), .in_5(in_15), .out_6(shift_aux_12_out_6));
  shift_aux shift_aux_13 (
    .B(B), .A(shift_aux_12_out_6), .current(in_10), .in_4(in_14), .in_5(in_15), .out_6(shift_aux_13_out_6));
  shift_aux shift_aux_14 (
    .B(B), .A(shift_aux_13_out_6), .current(in_11), .in_4(in_14), .in_5(in_15), .out_6(shift_aux_14_out_6));
endmodule

module shift_aux (
  input  [4:0] B,
  input  [4:0] A,
  input  [4:0] current,
  input  in_4,
  input  in_5,
  output [4:0] out_6
);

  wire and_1_out, n5bit_comparator_1_a___b;

  _5bit_comparator u_5bit_comparator_1 (
    .left_less(in_4), .left_greater(in_4), .left_equal(in_5), .A___B(n5bit_comparator_1_a___b), .A(current),
    .B(B));  // open: A___B_2, A___B_3
  and and_1 (and_1_out, n5bit_comparator_1_a___b, in_5);
  shift_bit shift_bit_1 (.A(A), .out_2(out_6));
endmodule

module multiplier (
  input  in_1,
  input  in_2,
  input  in_3,
  input  in_4,
  input  in_5,
  output out_6,
  output out_7,
  output out_8,
  output out_9,
  output out_10,
  output out_11,
  output out_12,
  output out_13,
  output out_14
);

  wire and_2_out, and_3_out, and_4_out, and_5_out, and_6_out, and_7_out, and_8_out, and_9_out, and_10_out,
       and_11_out, and_12_out, and_13_out, and_14_out, and_15_out, and_16_out, and_17_out, and_18_out,
       and_19_out, and_20_out, and_21_out, and_22_out, and_23_out, and_24_out, full_adder_1_carry_out,
       full_adder_1_soma, full_adder_2_carry_out, full_adder_2_soma, full_adder_3_carry_out,
       full_adder_3_soma, full_adder_4_carry_out, full_adder_4_soma, full_adder_5_carry_out,
       full_adder_5_soma, full_adder_6_carry_out, full_adder_6_soma, full_adder_7_carry_out,
       full_adder_7_soma, full_adder_8_carry_out, full_adder_8_soma, full_adder_9_carry_out,
       full_adder_10_carry_out, full_adder_10_soma, full_adder_11_carry_out, full_adder_12_carry_out,
       half_adder_1_carry_out, half_adder_2_carry_out, half_adder_3_carry_out, half_adder_4_carry_out,
       half_adder_4_soma, half_adder_5_carry_out, half_adder_6_carry_out, half_adder_6_soma,
       half_adder_7_carry_out, half_adder_7_soma, half_adder_8_carry_out;

  and and_1 (out_14, in_5, in_5);
  and and_2 (and_2_out, in_5, in_4);
  half_adder half_adder_1 (.A(and_2_out), .B(and_2_out), .Carry_out(half_adder_1_carry_out), .Soma(out_13));
  and and_3 (and_3_out, in_4, in_4);
  and and_4 (and_4_out, in_5, in_3);
  full_adder full_adder_1 (
    .A(and_4_out), .B(and_3_out), .Carry_in(half_adder_1_carry_out), .Carry_out(full_adder_1_carry_out),
    .Soma(full_adder_1_soma));
  and and_5 (and_5_out, in_3, in_5);
  half_adder half_adder_2 (.A(and_5_out), .B(full_adder_1_soma), .Carry_out(half_adder_2_carry_out), .Soma(out_12));
  and and_6 (and_6_out, in_2, in_5);
  and and_7 (and_7_out, in_3, in_4);
  full_adder full_adder_2 (
    .A(and_6_out), .B(and_7_out), .Carry_in(full_adder_1_carry_out), .Carry_out(full_adder_2_carry_out),
    .Soma(full_adder_2_soma));
  and and_8 (and_8_out, in_3, in_4);
  full_adder full_adder_3 (
    .A(full_adder_2_soma), .B(and_8_out), .Carry_in(half_adder_2_carry_out),
    .Carry_out(full_adder_3_carry_out), .Soma(full_adder_3_soma));
  and and_9 (and_9_out, in_1, in_5);
  full_adder full_adder_4 (
    .A(and_9_out), .B(and_12_out), .Carry_in(full_adder_2_carry_out), .Carry_out(full_adder_4_carry_out),
    .Soma(full_adder_4_soma));
  and and_10 (and_10_out, in_3, in_3);
  full_adder full_adder_5 (
    .A(and_10_out), .B(full_adder_4_soma), .Carry_in(full_adder_3_carry_out),
    .Carry_out(full_adder_5_carry_out), .Soma(full_adder_5_soma));
  and and_11 (and_11_out, in_2, in_5);
  half_adder half_adder_3 (.A(full_adder_3_soma), .B(and_11_out), .Carry_out(half_adder_3_carry_out), .Soma(out_11));
  and and_12 (and_12_out, in_2, in_4);
  and and_13 (and_13_out, in_3, in_2);
  and and_14 (and_14_out, in_4, in_2);
  full_adder full_adder_6 (
    .A(full_adder_5_soma), .B(and_14_out), .Carry_in(half_adder_3_carry_out),
    .Carry_out(full_adder_6_carry_out), .Soma(full_adder_6_soma));
  and and_15 (and_15_out, in_5, in_1);
  and and_16 (and_16_out, in_4, in_1);
  half_adder half_adder_4 (
    .A(full_adder_4_carry_out), .B(and_16_out), .Carry_out(half_adder_4_carry_out), .Soma(half_adder_4_soma));
  full_adder full_adder_7 (
    .A(and_13_out), .B(half_adder_4_soma), .Carry_in(full_adder_5_carry_out),
    .Carry_out(full_adder_7_carry_out), .Soma(full_adder_7_soma));
  and and_17 (and_17_out, in_2, in_3);
  half_adder half_adder_5 (.A(and_15_out), .B(full_adder_6_soma), .Carry_out(half_adder_5_carry_out), .Soma(out_10));
  and and_18 (and_18_out, in_3, in_1);
  half_adder half_adder_6 (
    .A(and_18_out), .B(full_adder_7_carry_out), .Carry_out(half_adder_6_carry_out), .Soma(half_adder_6_soma));
  and and_19 (and_19_out, in_2, in_2);
  full_adder full_adder_8 (
    .A(and_17_out), .B(full_adder_7_soma), .Carry_in(full_adder_6_carry_out),
    .Carry_out(full_adder_8_carry_out), .Soma(full_adder_8_soma));
  and and_20 (and_20_out, in_4, in_1);
  full_adder full_adder_9 (
    .A(and_20_out), .B(full_adder_8_soma), .Carry_in(half_adder_5_carry_out),
    .Carry_out(full_adder_9_carry_out), .Soma(out_9));
  full_adder full_adder_10 (
    .A(and_19_out), .B(full_adder_8_carry_out), .Carry_in(half_adder_6_soma),
    .Carry_out(full_adder_10_carry_out), .Soma(full_adder_10_soma));
  and and_21 (and_21_out, in_1, in_3);
  and and_22 (and_22_out, in_2, in_1);
  half_adder half_adder_7 (
    .A(full_adder_10_carry_out), .B(and_22_out), .Carry_out(half_adder_7_carry_out), .Soma(half_adder_7_soma));
  full_adder full_adder_11 (
    .A(full_adder_10_soma), .B(and_21_out), .Carry_in(full_adder_9_carry_out),
    .Carry_out(full_adder_11_carry_out), .Soma(out_8));
  and and_23 (and_23_out, in_2, in_1);
  full_adder full_adder_12 (
    .A(half_adder_7_soma), .B(and_23_out), .Carry_in(full_adder_11_carry_out),
    .Carry_out(full_adder_12_carry_out), .Soma(out_7));
  and and_24 (and_24_out, in_1, in_1);
  half_adder half_adder_8 (
    .A(full_adder_12_carry_out), .B(and_24_out), .Carry_out(half_adder_8_carry_out), .Soma(out_6));
endmodule

module reg_3_ff (
  input  [2:0] D2_D1_D0,
  input  CLOCK,
  output [2:0] Q2_Q1_Q0
);

  D_Flip_Flop d_ff_1 (.clk(CLOCK), .D(D2_D1_D0[2]), .Q(Q2_Q1_Q0[2]));  // open: Qn, preset, en, reset
  D_Flip_Flop d_ff_2 (.clk(CLOCK), .D(D2_D1_D0[1]), .Q(Q2_Q1_Q0[1]));  // open: Qn, preset, en, reset
  D_Flip_Flop d_ff_3 (.clk(CLOCK), .D(D2_D1_D0[0]), .Q(Q2_Q1_Q0[0]));  // open: Qn, preset, en, reset
endmodule

module multiplexer_3_bits (
  input  [15:0] A,
  input  [15:0] B,
  input  LOAD,
  output [15:0] SAIDA
);

  _2x1_multiplexer u_2x1_multiplexer_1 (.A(B[0]), .B(A[0]), .Seletor(LOAD), .out_4(SAIDA[0]));
  _2x1_multiplexer u_2x1_multiplexer_2 (.A(B[1]), .B(A[1]), .Seletor(LOAD), .out_4(SAIDA[1]));
  _2x1_multiplexer u_2x1_multiplexer_3 (.A(B[2]), .B(A[2]), .Seletor(LOAD), .out_4(SAIDA[2]));
  _2x1_multiplexer u_2x1_multiplexer_4 (.A(B[3]), .B(A[3]), .Seletor(LOAD), .out_4(SAIDA[3]));
  _2x1_multiplexer u_2x1_multiplexer_5 (.A(B[4]), .B(A[4]), .Seletor(LOAD), .out_4(SAIDA[4]));
  _2x1_multiplexer u_2x1_multiplexer_6 (.A(B[5]), .B(A[5]), .Seletor(LOAD), .out_4(SAIDA[5]));
  _2x1_multiplexer u_2x1_multiplexer_7 (.A(B[6]), .B(A[6]), .Seletor(LOAD), .out_4(SAIDA[6]));
  _2x1_multiplexer u_2x1_multiplexer_8 (.A(B[7]), .B(A[7]), .Seletor(LOAD), .out_4(SAIDA[7]));
  _2x1_multiplexer u_2x1_multiplexer_9 (.A(B[8]), .B(A[8]), .Seletor(LOAD), .out_4(SAIDA[8]));
  _2x1_multiplexer u_2x1_multiplexer_10 (.A(B[9]), .B(A[9]), .Seletor(LOAD), .out_4(SAIDA[9]));
  _2x1_multiplexer u_2x1_multiplexer_11 (.A(B[10]), .B(A[10]), .Seletor(LOAD), .out_4(SAIDA[10]));
  _2x1_multiplexer u_2x1_multiplexer_12 (.A(B[11]), .B(A[11]), .Seletor(LOAD), .out_4(SAIDA[11]));
  _2x1_multiplexer u_2x1_multiplexer_13 (.A(B[12]), .B(A[12]), .Seletor(LOAD), .out_4(SAIDA[12]));
  _2x1_multiplexer u_2x1_multiplexer_14 (.A(B[13]), .B(A[13]), .Seletor(LOAD), .out_4(SAIDA[13]));
  _2x1_multiplexer u_2x1_multiplexer_15 (.A(B[14]), .B(A[14]), .Seletor(LOAD), .out_4(SAIDA[14]));
  _2x1_multiplexer u_2x1_multiplexer_16 (.A(B[15]), .B(A[15]), .Seletor(LOAD), .out_4(SAIDA[15]));
endmodule

module control_block (
  input  \começa ,
  input  compara,
  input  compara_LSB,
  output RI,
  output RP,
  output mux,
  output L_ANDO,
  output L_DOR,
  output CI,
  output LP
);

  wire and_1_out, and_2_out, and_3_out, and_4_out, and_5_out, and_6_out, and_7_out, and_8_out, and_9_out,
       clock_1_out, not_1_out, not_2_out, not_3_out, not_4_out, not_5_out, not_6_out, not_7_out, not_8_out,
       not_9_out, not_10_out, not_11_out, not_12_out, not_13_out, not_14_out, not_15_out, not_16_out,
       not_17_out, not_18_out, not_19_out, not_20_out, not_21_out, not_22_out, not_23_out, not_24_out;
  wire [2:0] or_1_out, reg_3_ff_1_q2_q1_q0;

  not not_1 (not_1_out, reg_3_ff_1_q2_q1_q0[0]);
  not not_2 (not_2_out, compara);
  not not_3 (not_3_out, reg_3_ff_1_q2_q1_q0[0]);
  not not_4 (not_4_out, compara_LSB);
  not not_5 (not_5_out, reg_3_ff_1_q2_q1_q0[0]);
  not not_6 (not_6_out, reg_3_ff_1_q2_q1_q0[0]);
  not not_7 (not_7_out, reg_3_ff_1_q2_q1_q0[1]);
  not not_8 (not_8_out, reg_3_ff_1_q2_q1_q0[1]);
  not not_9 (not_9_out, reg_3_ff_1_q2_q1_q0[2]);
  not not_10 (not_10_out, reg_3_ff_1_q2_q1_q0[0]);
  not not_11 (not_11_out, reg_3_ff_1_q2_q1_q0[2]);
  not not_12 (not_12_out, reg_3_ff_1_q2_q1_q0[0]);
  not not_13 (not_13_out, reg_3_ff_1_q2_q1_q0[1]);
  not not_14 (not_14_out, reg_3_ff_1_q2_q1_q0[2]);
  not not_15 (not_15_out, reg_3_ff_1_q2_q1_q0[0]);
  not not_16 (not_16_out, reg_3_ff_1_q2_q1_q0[2]);
  not not_17 (not_17_out, compara);
  not not_18 (not_18_out, reg_3_ff_1_q2_q1_q0[0]);
  not not_19 (not_19_out, reg_3_ff_1_q2_q1_q0[2]);
  and and_1 (and_1_out, not_1_out, reg_3_ff_1_q2_q1_q0[1], not_2_out);
  and and_2 (and_2_out, not_3_out, reg_3_ff_1_q2_q1_q0[1], not_4_out);
  and and_3 (and_3_out, not_5_out, reg_3_ff_1_q2_q1_q0[1], reg_3_ff_1_q2_q1_q0[2]);
  and and_4 (and_4_out, not_6_out, not_7_out, reg_3_ff_1_q2_q1_q0[2]);
  and and_5 (and_5_out, reg_3_ff_1_q2_q1_q0[0], not_8_out, not_9_out);
  and and_6 (and_6_out, not_10_out, compara, reg_3_ff_1_q2_q1_q0[1], compara_LSB, not_11_out);
  and and_7 (and_7_out, not_12_out, not_13_out, not_14_out, \começa );
  and and_8 (and_8_out, not_15_out, reg_3_ff_1_q2_q1_q0[1], not_16_out, not_17_out);
  and and_9 (and_9_out, not_18_out, reg_3_ff_1_q2_q1_q0[1], not_19_out, compara_LSB);
  or or_1 (or_1_out[0], and_1_out, and_2_out, and_3_out);
  or or_2 (or_1_out[1], and_4_out, and_5_out, and_6_out);
  or or_3 (or_1_out[2], and_7_out, and_8_out, and_9_out);
  reg_3_ff reg_3_ff_1 (.D2_D1_D0(or_1_out), .CLOCK(clock_1_out), .Q2_Q1_Q0(reg_3_ff_1_q2_q1_q0));
  Clock clock_1 (.out(clock_1_out));
  not not_20 (not_20_out, reg_3_ff_1_q2_q1_q0[0]);
  not not_21 (not_21_out, reg_3_ff_1_q2_q1_q0[1]);
  not not_22 (not_22_out, reg_3_ff_1_q2_q1_q0[1]);
  not not_23 (not_23_out, reg_3_ff_1_q2_q1_q0[2]);
  and and_10 (mux, not_20_out, not_21_out, reg_3_ff_1_q2_q1_q0[2]);
  and and_11 (CI, reg_3_ff_1_q2_q1_q0[0], not_22_out, not_23_out);
  not not_24 (not_24_out, reg_3_ff_1_q2_q1_q0[0]);
  and and_12 (LP, not_24_out, reg_3_ff_1_q2_q1_q0[1], reg_3_ff_1_q2_q1_q0[2]);
  or or_4 (L_ANDO, mux, CI);

  assign L_DOR = L_ANDO;
  assign RI = mux;
  assign RP = mux;
endmodule

module shift_bit_right (
  input  [15:0] A,
  output [15:0] out_2
);

  D_Flip_Flop d_ff_1 (.clk(A[15]), .Q(out_2[0]));  // open: D, Qn, preset, en, reset

  assign out_2[15:1] = A[14:0];
endmodule

module shift_bit_left (
  input  [15:0] A,
  output [15:0] out_2
);

  D_Flip_Flop d_ff_1 (.clk(A[0]), .Q(out_2[15]));  // open: D, Qn, preset, en, reset

  assign out_2[14:0] = A[15:1];
endmodule

module reg_16_ff (
  input  RESET_REG,
  input  [15:0] in_2,
  input  LOAD_REG
);

  wire clock_1_out;
  wire [15:0] d_ff_1_q, multiplexer_3_bits_1_saida;

  Clock clock_1 (.out(clock_1_out));
  D_Flip_Flop d_ff_1 (
    .clk(clock_1_out), .D(multiplexer_3_bits_1_saida[0]), .Q(d_ff_1_q[0]), .reset(RESET_REG));  // open: Qn, preset, en
  D_Flip_Flop d_ff_2 (
    .clk(clock_1_out), .D(multiplexer_3_bits_1_saida[4]), .Q(d_ff_1_q[4]), .reset(RESET_REG));  // open: Qn, preset, en
  D_Flip_Flop d_ff_3 (
    .clk(clock_1_out), .D(multiplexer_3_bits_1_saida[8]), .Q(d_ff_1_q[8]), .reset(RESET_REG));  // open: Qn, preset, en
  D_Flip_Flop d_ff_4 (
    .clk(clock_1_out), .D(multiplexer_3_bits_1_saida[12]), .Q(d_ff_1_q[12]), .reset(RESET_REG));  // open: Qn, preset, en
  D_Flip_Flop d_ff_5 (
    .clk(clock_1_out), .D(multiplexer_3_bits_1_saida[1]), .Q(d_ff_1_q[1]), .reset(RESET_REG));  // open: Qn, preset, en
  D_Flip_Flop d_ff_6 (
    .clk(clock_1_out), .D(multiplexer_3_bits_1_saida[5]), .Q(d_ff_1_q[5]), .reset(RESET_REG));  // open: Qn, preset, en
  D_Flip_Flop d_ff_7 (
    .clk(clock_1_out), .D(multiplexer_3_bits_1_saida[9]), .Q(d_ff_1_q[9]), .reset(RESET_REG));  // open: Qn, preset, en
  D_Flip_Flop d_ff_8 (
    .clk(clock_1_out), .D(multiplexer_3_bits_1_saida[13]), .Q(d_ff_1_q[13]), .reset(RESET_REG));  // open: Qn, preset, en
  D_Flip_Flop d_ff_9 (
    .clk(clock_1_out), .D(multiplexer_3_bits_1_saida[2]), .Q(d_ff_1_q[2]), .reset(RESET_REG));  // open: Qn, preset, en
  D_Flip_Flop d_ff_10 (
    .clk(clock_1_out), .D(multiplexer_3_bits_1_saida[6]), .Q(d_ff_1_q[6]), .reset(RESET_REG));  // open: Qn, preset, en
  D_Flip_Flop d_ff_11 (
    .clk(clock_1_out), .D(multiplexer_3_bits_1_saida[10]), .Q(d_ff_1_q[10]), .reset(RESET_REG));  // open: Qn, preset, en
  D_Flip_Flop d_ff_12 (
    .clk(clock_1_out), .D(multiplexer_3_bits_1_saida[14]), .Q(d_ff_1_q[14]), .reset(RESET_REG));  // open: Qn, preset, en
  D_Flip_Flop d_ff_13 (
    .clk(clock_1_out), .D(multiplexer_3_bits_1_saida[3]), .Q(d_ff_1_q[3]), .reset(RESET_REG));  // open: Qn, preset, en
  D_Flip_Flop d_ff_14 (
    .clk(clock_1_out), .D(multiplexer_3_bits_1_saida[7]), .Q(d_ff_1_q[7]), .reset(RESET_REG));  // open: Qn, preset, en
  D_Flip_Flop d_ff_15 (
    .clk(clock_1_out), .D(multiplexer_3_bits_1_saida[11]), .Q(d_ff_1_q[11]), .reset(RESET_REG));  // open: Qn, preset, en
  D_Flip_Flop d_ff_16 (
    .clk(clock_1_out), .D(multiplexer_3_bits_1_saida[15]), .Q(d_ff_1_q[15]), .reset(RESET_REG));  // open: Qn, preset, en
  multiplexer_3_bits multiplexer_3_bits_1 (.LOAD(LOAD_REG), .A(in_2), .B(d_ff_1_q), .SAIDA(multiplexer_3_bits_1_saida));
endmodule

module contador (
  input  in_1,
  input  in_2,
  input  [7:0] _00000001,
  output [7:0] out_4
);

  wire [7:0] n5bit_adder_1_output;

  D_Flip_Flop d_ff_1 (.clk(in_1), .D(n5bit_adder_1_output[0]), .Q(out_4[0]), .reset(in_2));  // open: Qn, preset, en
  D_Flip_Flop d_ff_2 (.clk(in_1), .D(n5bit_adder_1_output[4]), .Q(out_4[4]), .reset(in_2));  // open: Qn, preset, en
  D_Flip_Flop d_ff_3 (.clk(in_1), .D(n5bit_adder_1_output[1]), .Q(out_4[1]), .reset(in_2));  // open: Qn, preset, en
  D_Flip_Flop d_ff_4 (.clk(in_1), .D(n5bit_adder_1_output[5]), .Q(out_4[5]), .reset(in_2));  // open: Qn, preset, en
  D_Flip_Flop d_ff_5 (.clk(in_1), .D(n5bit_adder_1_output[2]), .Q(out_4[2]), .reset(in_2));  // open: Qn, preset, en
  D_Flip_Flop d_ff_6 (.clk(in_1), .D(n5bit_adder_1_output[6]), .Q(out_4[6]), .reset(in_2));  // open: Qn, preset, en
  D_Flip_Flop d_ff_7 (.clk(in_1), .D(n5bit_adder_1_output[3]), .Q(out_4[3]), .reset(in_2));  // open: Qn, preset, en
  D_Flip_Flop d_ff_8 (.clk(in_1), .D(n5bit_adder_1_output[7]), .Q(out_4[7]), .reset(in_2));  // open: Qn, preset, en
  _5bit_adder u_5bit_adder_1 (.\output (n5bit_adder_1_output), .A(out_4), .B(_00000001));
endmodule
